// Digital circuit 4bit_adder.dig as structural Verilog
module _4bit_adder (
  input  in_1
);

  wire full_adder_1_p1, full_adder_1_p3, full_adder_2_p2, full_adder_3_p2;

  // full_adder full_adder_1: pin names not known; wires that end beside it: full_adder_1_p1, full_adder_1_p1, full_adder_1_p3
  // full_adder full_adder_2: pin names not known; wires that end beside it: full_adder_1_p3, full_adder_2_p2
  // full_adder full_adder_3: pin names not known; wires that end beside it: full_adder_2_p2, full_adder_3_p2
  // full_adder full_adder_4: pin names not known; wires that end beside it: full_adder_3_p2, in_1
endmodule
