// Digital circuit 6Bit_and.dig as structural Verilog
module _6Bit_and (
  input  [2:0] A_3,
  input  [2:0] B_3,
  input  [2:0] A_4,
  input  [2:0] B_4,
  output out_1
);

  wire and_1_out, and_2_out, and_3_out, and_4_out, and_5_out, and_6_out, and_7_out, and_8_out, and_9_out,
       and_10_out;

  and and_1 (and_1_out, A_3[0], B_3[0]);
  and and_2 (and_2_out, A_3[1], B_3[1]);
  and and_3 (and_3_out, A_3[2], B_3[2]);
  and and_4 (and_4_out, A_4[0], B_4[0]);
  and and_5 (and_5_out, A_4[1], B_4[1]);
  and and_6 (and_6_out, A_4[2], B_4[2]);
  and and_7 (and_7_out, and_1_out, and_2_out);
  and and_8 (and_8_out, and_4_out, and_5_out);
  and and_9 (and_9_out, and_7_out, and_3_out);
  and and_10 (and_10_out, and_8_out, and_6_out);
  and and_11 (out_1, and_9_out, and_10_out);
endmodule
