// Digital circuit 8 bit adder.dig as structural Verilog
module _8_bit_adder (
);

  wire full_adder_1_carry_out, full_adder_1_sum_out, full_adder_2_sum_out, full_adder_3_carry_out,
       full_adder_3_sum_out, full_adder_4_sum_out, full_adder_5_sum_out, full_adder_6_carry_out,
       full_adder_6_sum_out, full_adder_7_carry_out, full_adder_7_sum_out, full_adder_8_carry_out,
       full_adder_8_sum_out, undriven, undriven_2, undriven_3, undriven_4, undriven_5, undriven_6,
       undriven_7, undriven_8, undriven_9, undriven_10, undriven_11, undriven_12, undriven_13, undriven_14,
       undriven_15;

  full_adder full_adder_1 (
    .Carry_in(full_adder_2_sum_out), .A_in(undriven_2), .B_in(undriven), .Carry_out(full_adder_1_carry_out),
    .Sum_out(full_adder_1_sum_out));
  full_adder full_adder_2 (
    .Carry_in(full_adder_3_sum_out), .A_in(undriven_4), .B_in(undriven_3), .Sum_out(full_adder_2_sum_out));  // open: Carry_out
  full_adder full_adder_3 (
    .Carry_in(full_adder_4_sum_out), .A_in(undriven_6), .B_in(undriven_5),
    .Carry_out(full_adder_3_carry_out), .Sum_out(full_adder_3_sum_out));
  full_adder full_adder_4 (
    .Carry_in(full_adder_5_sum_out), .A_in(undriven_8), .B_in(undriven_7), .Sum_out(full_adder_4_sum_out));  // open: Carry_out
  full_adder full_adder_5 (
    .Carry_in(full_adder_6_sum_out), .A_in(undriven_10), .B_in(undriven_9), .Sum_out(full_adder_5_sum_out));  // open: Carry_out
  full_adder full_adder_6 (
    .Carry_in(full_adder_7_sum_out), .A_in(undriven_12), .B_in(undriven_11),
    .Carry_out(full_adder_6_carry_out), .Sum_out(full_adder_6_sum_out));
  full_adder full_adder_7 (
    .Carry_in(full_adder_8_sum_out), .Carry_out(full_adder_7_carry_out), .Sum_out(full_adder_7_sum_out));  // open: A_in, B_in
  full_adder full_adder_8 (
    .Carry_in(undriven_15), .A_in(undriven_14), .B_in(undriven_13), .Carry_out(full_adder_8_carry_out),
    .Sum_out(full_adder_8_sum_out));
endmodule
