// Digital circuit full_adder.dig as structural Verilog
module full_adder (
  input  Carry_in,
  input  A_in,
  input  B_in,
  output Carry_out,
  output Sum_out
);

  wire half_adder_1_carry_out, half_adder_1_sum_out, half_adder_2_carry_out;

  half_adder half_adder_1 (
    .A_in(A_in), .B_in(B_in), .Sum_out(half_adder_1_sum_out), .Carry_out(half_adder_1_carry_out));
  half_adder half_adder_2 (
    .A_in(Carry_in), .B_in(half_adder_1_sum_out), .Sum_out(Sum_out), .Carry_out(half_adder_2_carry_out));
  or or_1 (Carry_out, half_adder_2_carry_out, half_adder_1_carry_out);
endmodule
