// Digital circuit half_adder.dig as structural Verilog
module half_adder (
  input  A_in,
  input  B_in,
  output Sum_out,
  output Carry_out
);

  xor xor_1 (Sum_out, A_in, B_in);
  and and_1 (Carry_out, A_in, B_in);
endmodule
